# Fritzing sketch AMD Device_Circuit (saved by Fritzing 0.9.2b)
breadboards: 1

parts:
  Part1 = Arduino Uno (Rev3)
  U1 = NodeMCU V1.0  # not connected
  Display1 = LCD screen 16x2 IIC [part_number=101290]
  Mod1 = MQ-7 breakout
  F1 = Fan - Ventilador [package=THT]
  M1 = L293D Motor Driver
  VCC1 = Battery block 9V  # not connected
  J1 = Piezo Speaker
  Part4 = DC-DC Power Module (5v)  # not connected
  Part5 = Lilypad Battery Connect
  Part6 = DC-DC Power Module (5v)
  DHT11_1 = DHT11 module

nets:
  N1: Part1.A0, Mod1.AO
  N2: Part1.A4/SDA, Display1.SDA
  N3: Part1.A5/SCL, Display1.SCL
  N4: Part1.D9_PWM, J1.pin2
  N5: Part1.D3_PWM, DHT11_1.VCC
  N6: Part1.D4, M1.pin_5
  VCC: Part1.5V, Display1.VCC, Mod1.VCC, DHT11_1.DATA
  GND: Part1.GND, Display1.GND, Mod1.GND, M1.pin_6, J1.pin1, Part6.GND*, DHT11_1.GND
  N7: Part1.VIN, Part6.Vout
  N8: F1.5V, M1.pin_9
  N9: F1.GND, M1.pin_10
  N10: Part5.-, Part6.GND
  N11: Part5.+, Part6.Vin

notes:
  Fan/Exhaust
  L293D
  9V Battery
  MQ6 Gas sensor
  LCD Display// I2C
  DHT11
  Buzzer
  UNO
  AC 230V
  Adapter

custom parts:
  NodeMCU V1.0: ESP8266 based NodeMCU
  LCD screen 16x2 IIC: LCD screen with HD44780 controller enables showing text, symbols, value or anything else that comes from Croduino/Arduino. It is capable of showing 16 symbols in two lines and therefore can be used in many projects that need to send clearly visible and legible output information.. • Color of symbols: White • Backlight: Blue • Dimensions: 80 x 36 x 12 mm • Screen dimensions: 64.5 x 16 mm •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
  MQ-7 breakout: MQ-5 gas sensor
  Fan - Ventilador: Ventilador de 2 pines, se encuentra comunmente en computadoras de escritorio
  DC-DC Power Module (5v): DC-DC Power Module based con AMS1117-5.0 Input: DC 6~12V (input power must higher 1V than output power); Output: 5V (+/-0.05V error), 800mA
  DHT11 module: DHT11 black pcb module
